# Fritzing sketch wiring-diagram (saved by Fritzing 0.9.4)

parts:
  A1 = ESP32 devkit 38p expansion board
  U1 = ESP32-38PinWide [part_number=ESP32-38PinWide]  # not connected
  A2 = GY-BMP280 Breakout
  Bat1 = battery_holder_single_18650
  TP1 = TP4056 [chip_label=TP4056 package="DIP (Dual Inline) [THT]"]
  USBTTL1 = Micro USB B Plug
  M1 = INA219 DC Current Monitor Module [part_number=CJMCU]  # not connected

nets:
  N1: A1.Pin_50, A1.Pin_51, A1.Pin_144, A2.Pin_2, A2.Pin_6
  N2: A1.Pin_58, A1.Pin_59, A2.Pin_1, A2.Pin_5
  N3: A1.Pin_174, A2.Pin_4
  N4: A1.Pin_177, A2.Pin_3
  N5: Bat1.+#0, TP1.pin5
  N6: Bat1.+#1, TP1.pin4
  N7: TP1.pin3, TP1.pin6, USBTTL1.usb

custom parts:
  ESP32 devkit 38p expansion board: Upgraded ESP32 38P Development ESP32-DevKitC-32 ESP-WROOM-32 Expansion Board.
  ESP32-38PinWide: Generic 38-Pin ESP32 with wide format (only access to one side of pins on a breadboard) based on Stephen Lilley's HiLetgo ESP-WROOM-32 ESP32 ESP-32S Development Board.
  battery_holder_single_18650: single 18650 battery holder
  TP4056: A DIP stand-in part for whatever IC you want. With 6 pins on a 300mil dual inline package (DIP) footprint.
  INA219 DC Current Monitor Module: INA219 DC Current Monitor Module Links: INA219 product information
